// Logisim project adder.circ as structural Verilog: 1 circuit, main circuit main
module main (
  input  [15:0] in_1,
  input  [15:0] in_2
);

  wire undriven, undriven_2, undriven_3, undriven_4;
  wire [3:0] adder_1_out_2, adder_1_out_3;
  wire [7:0] adder_1_out;

  Hex_Digit_Display hex_digit_display_1 (.value(in_1[15:12]));  // open: dp
  Hex_Digit_Display hex_digit_display_2 (.value(in_1[11:8]));  // open: dp
  Hex_Digit_Display hex_digit_display_3 (.value(in_1[7:4]));  // open: dp
  Hex_Digit_Display hex_digit_display_4 (.value(in_1[3:0]));  // open: dp
  Hex_Digit_Display hex_digit_display_5 (.value(in_2[15:12]));  // open: dp
  Hex_Digit_Display hex_digit_display_6 (.value(in_2[11:8]));  // open: dp
  Adder #(.width(16)) adder_1 (
    .a(in_1), .b(in_2), .out({adder_1_out_3, adder_1_out_2, adder_1_out}));  // open: cin, cout
  Hex_Digit_Display hex_digit_display_7 (.value(in_2[3:0]));  // open: dp
  Hex_Digit_Display hex_digit_display_8 (.value(in_2[7:4]));  // open: dp
  Hex_Digit_Display hex_digit_display_9 (.value(adder_1_out_2), .dp(undriven_2));
  Hex_Digit_Display hex_digit_display_10 (.value(adder_1_out_3), .dp(undriven));
  LED led_1 (.in(undriven_2));
  LED led_2 (.in(undriven));
  Hex_Digit_Display hex_digit_display_11 (.value(adder_1_out[7:4]), .dp(undriven_3));
  Hex_Digit_Display hex_digit_display_12 (.value(adder_1_out[3:0]), .dp(undriven_4));
  LED led_3 (.in(undriven_4));
  LED led_4 (.in(undriven_3));

  // Notes on the sheet:
  //   +
  //   =
endmodule
