// Logisim project deam.circ as structural Verilog: 1 circuit, main circuit main
module main (
);

  wire clock_1_out, not_1_out;
  wire [3:0] bit_extender_1_out;

  Clock clock_1 (.out(clock_1_out));
  not not_1 (not_1_out, clock_1_out);
  assign bit_extender_1_out = {{3{1'b0}}, not_1_out};  // Bit_Extender bit_extender_1
  Hex_Digit_Display hex_digit_display_1 (.value(bit_extender_1_out));  // open: dp
  LED led_1 (.in(clock_1_out));
  LED led_2 (.in(not_1_out));
  LED led_3 (.in(clock_1_out));
  LED led_4 (.in(not_1_out));
  LED led_5 (.in(clock_1_out));
  LED led_6 (.in(not_1_out));
  LED led_7 (.in(clock_1_out));
  LED led_8 (.in(not_1_out));
  LED led_9 (.in(clock_1_out));
  LED led_10 (.in(not_1_out));
  LED led_11 (.in(clock_1_out));
  LED led_12 (.in(not_1_out));
  LED led_13 (.in(clock_1_out));
  LED led_14 (.in(not_1_out));
  LED led_15 (.in(clock_1_out));
  LED led_16 (.in(not_1_out));
  LED led_17 (.in(clock_1_out));
  LED led_18 (.in(not_1_out));
  LED led_19 (.in(clock_1_out));
  LED led_20 (.in(not_1_out));
  LED led_21 (.in(clock_1_out));
  LED led_22 (.in(not_1_out));
  LED led_23 (.in(clock_1_out));
  LED led_24 (.in(not_1_out));
  LED led_25 (.in(clock_1_out));
  LED led_26 (.in(not_1_out));
  LED led_27 (.in(clock_1_out));
  LED led_28 (.in(not_1_out));
  LED led_29 (.in(clock_1_out));
  LED led_30 (.in(not_1_out));
  LED led_31 (.in(clock_1_out));
  LED led_32 (.in(not_1_out));
  LED led_33 (.in(clock_1_out));
  LED led_34 (.in(not_1_out));
  LED led_35 (.in(clock_1_out));
  LED led_36 (.in(not_1_out));
  LED led_37 (.in(clock_1_out));
  LED led_38 (.in(not_1_out));
  LED led_39 (.in(clock_1_out));
  LED led_40 (.in(not_1_out));
  LED led_41 (.in(clock_1_out));
  LED led_42 (.in(not_1_out));
  LED led_43 (.in(clock_1_out));
  LED led_44 (.in(not_1_out));
  LED led_45 (.in(clock_1_out));
  LED led_46 (.in(not_1_out));
  LED led_47 (.in(clock_1_out));
  LED led_48 (.in(not_1_out));
  LED led_49 (.in(clock_1_out));
  LED led_50 (.in(not_1_out));
  LED led_51 (.in(clock_1_out));
  LED led_52 (.in(not_1_out));
  LED led_53 (.in(clock_1_out));
  LED led_54 (.in(not_1_out));
  LED led_55 (.in(clock_1_out));
  LED led_56 (.in(not_1_out));
endmodule
