// Logisim project digit.circ as structural Verilog: 1 circuit, main circuit main
module main (
);

  wire button_1_out, button_2_out, button_3_out, button_4_out, button_5_out, button_6_out, button_7_out,
       button_8_out, button_9_out, button_10_out;
  wire [3:3] transistor_5_out;
  wire [5:0] transistor_1_out;
  wire [6:2] transistor_10_out;

  Transistor #(.\type ("n"), .width(6)) transistor_1 (.in({6{1'b1}}), .out(transistor_1_out), .gate(button_1_out));
  Button button_1 (.out(button_1_out));
  _7_Segment_Display u_7_segment_display_1 (
    .g(transistor_10_out[6]), .f(transistor_1_out[5]), .a(transistor_1_out[1]), .b(transistor_1_out[2]),
    .e(transistor_1_out[4]), .d(transistor_1_out[3]), .c(transistor_1_out[0]));  // open: dp
  Button button_2 (.out(button_2_out));
  Button button_3 (.out(button_3_out));
  Button button_4 (.out(button_4_out));
  Button button_5 (.out(button_5_out));
  Transistor #(.\type ("n"), .width(2)) transistor_2 (
    .in(2'b11), .out({transistor_1_out[2], transistor_1_out[0]}), .gate(button_3_out));
  Button button_6 (.out(button_6_out));
  Button button_7 (.out(button_7_out));
  Button button_8 (.out(button_8_out));
  Button button_9 (.out(button_9_out));
  Transistor #(.\type ("n"), .width(5)) transistor_3 (
    .in({5{1'b1}}),
    .out({transistor_1_out[1], transistor_1_out[2], transistor_1_out[3], transistor_1_out[4], transistor_10_out[6]}),
    .gate(button_4_out));
  Transistor #(.\type ("n"), .width(5)) transistor_4 (
    .in({5{1'b1}}),
    .out({transistor_1_out[1], transistor_1_out[2], transistor_1_out[0], transistor_1_out[3], transistor_10_out[6]}),
    .gate(button_5_out));
  Transistor #(.\type ("n"), .width(5)) transistor_5 (
    .in({5{1'b1}}),
    .out({transistor_1_out[2], transistor_5_out[3], transistor_1_out[0], transistor_10_out[6], transistor_1_out[5]}),
    .gate(button_2_out));
  Transistor #(.\type ("n"), .width(5)) transistor_6 (
    .in({5{1'b1}}),
    .out({transistor_1_out[1:0], transistor_1_out[3], transistor_10_out[6], transistor_1_out[5]}),
    .gate(button_7_out));
  Transistor #(.\type ("n"), .width(6)) transistor_7 (
    .in({6{1'b1}}),
    .out({transistor_1_out[1:0], transistor_1_out[3], transistor_1_out[4], transistor_10_out[6], transistor_1_out[5]}),
    .gate(button_6_out));
  Transistor #(.\type ("n"), .width(3)) transistor_8 (
    .in(3'b111), .out({transistor_1_out[1], transistor_1_out[2], transistor_1_out[0]}), .gate(button_9_out));
  Transistor #(.\type ("n"), .width(5)) transistor_9 (
    .in({5{1'b1}}),
    .out({transistor_1_out[1], transistor_1_out[2], transistor_1_out[0], transistor_10_out[6], transistor_1_out[5]}),
    .gate(button_10_out));
  Transistor #(.\type ("n"), .width(8)) transistor_10 (
    .in({8{1'b1}}),
    .out({transistor_1_out[5], transistor_10_out[6], transistor_1_out[4:3], transistor_1_out[0], transistor_10_out[2], transistor_1_out[2:1]}),
    .gate(button_8_out));
  Button button_10 (.out(button_10_out));
endmodule
